// Logisim project circuit1.circ as structural Verilog
module main (
  input  [15:0] Numbers,
  output [15:0] Zero
);

  Subtractor #(.width(16)) subtractor_1 (.a(Numbers), .b(Numbers), .out(Zero));  // open: bin, bout
endmodule

module ChangeInput (
  input  [15:0] X,
  input  zx,
  input  nx,
  output [15:0] out_4
);

  wire [15:0] bitwisenegator_1_out_2, multiplexer_1_out, zero16_1_out_2;

  Zero16 zero16_1 (.in_1(X), .out_2(zero16_1_out_2));
  Multiplexer #(.width(16)) multiplexer_1 (.in0(X), .in1(zero16_1_out_2), .out(multiplexer_1_out), .sel(zx));
  Multiplexer #(.width(16)) multiplexer_2 (
    .in0(multiplexer_1_out), .in1(bitwisenegator_1_out_2), .out(out_4), .sel(nx));
  bitwiseNegator bitwisenegator_1 (.in_1(multiplexer_1_out), .out_2(bitwisenegator_1_out_2));
endmodule

module bitwiseNegator (
  input  [15:0] in_1,
  output [15:0] out_2
);

  wire [15:0] negator_1_out;

  Negator #(.width(16)) negator_1 (.in(16'h1), .out(negator_1_out));
  Subtractor #(.width(16)) subtractor_1 (.a(negator_1_out), .b(in_1), .out(out_2));  // open: bin, bout
endmodule

module Zero16 (
  input  [15:0] in_1,
  output [15:0] out_2
);

  Subtractor #(.width(16)) subtractor_1 (.a(in_1), .b(in_1), .out(out_2));  // open: bin, bout
endmodule

module ALU (
  input  [15:0] X,
  input  zx,
  input  nx,
  input  [15:0] Y,
  input  zy,
  input  ny,
  input  f,
  input  no,
  output [15:0] out_9
);

  wire [15:0] adder_1_out, bitwiseand16_1_out_3, bitwisenegator_1_out_2, changeinput_1_out_4,
       changeinput_2_out_4, multiplexer_1_out;

  ChangeInput changeinput_1 (.X(X), .zx(zx), .nx(nx), .out_4(changeinput_1_out_4));
  ChangeInput changeinput_2 (.X(Y), .zx(zy), .nx(ny), .out_4(changeinput_2_out_4));
  Adder #(.width(16)) adder_1 (.a(changeinput_1_out_4), .b(changeinput_2_out_4), .out(adder_1_out));  // open: cin, cout
  bitwiseAnd16 bitwiseand16_1 (.in_1(changeinput_1_out_4), .in_2(changeinput_2_out_4), .out_3(bitwiseand16_1_out_3));
  Multiplexer #(.width(16)) multiplexer_1 (
    .in0(bitwiseand16_1_out_3), .in1(adder_1_out), .out(multiplexer_1_out), .sel(f));
  Multiplexer #(.width(16)) multiplexer_2 (
    .in0(multiplexer_1_out), .in1(bitwisenegator_1_out_2), .out(out_9), .sel(no));
  bitwiseNegator bitwisenegator_1 (.in_1(multiplexer_1_out), .out_2(bitwisenegator_1_out_2));
endmodule

module bitwiseAnd16 (
  input  [15:0] in_1,
  input  [15:0] in_2,
  output [15:0] out_3
);

  and bit0 (out_3[0], in_1[0], in_2[0]);
  and bit1 (out_3[1], in_1[1], in_2[1]);
  and bit2 (out_3[2], in_1[2], in_2[2]);
  and bit3 (out_3[3], in_1[3], in_2[3]);
  and bit4 (out_3[4], in_1[4], in_2[4]);
  and bit5 (out_3[5], in_1[5], in_2[5]);
  and bit6 (out_3[6], in_1[6], in_2[6]);
  and bit7 (out_3[7], in_1[7], in_2[7]);
  and bit8 (out_3[8], in_1[8], in_2[8]);
  and bit9 (out_3[9], in_1[9], in_2[9]);
  and bit10 (out_3[10], in_1[10], in_2[10]);
  and bit11 (out_3[11], in_1[11], in_2[11]);
  and bit12 (out_3[12], in_1[12], in_2[12]);
  and bit13 (out_3[13], in_1[13], in_2[13]);
  and bit14 (out_3[14], in_1[14], in_2[14]);
  and bit15 (out_3[15], in_1[15], in_2[15]);
endmodule

module testALU (
  input  [15:0] X,
  input  [15:0] Y,
  input  zx,
  input  nz,
  input  zy,
  input  ny,
  input  f,
  input  no,
  output [15:0] out_9,
  output [15:0] out_10
);

  bitwiseAnd16 bitwiseand16_1 (.in_1(X), .in_2(Y), .out_3(out_9));
  ALU alu_1 (.X(X), .zx(zx), .nx(nz), .Y(Y), .zy(zy), .ny(ny), .f(f), .no(no), .out_9(out_10));
endmodule

module DFF (
  input  [15:0] in_1,
  input  in_2,
  output [15:0] out_3
);

  wire clock_1_out;

  Clock clock_1 (.out(clock_1_out));
  Register #(.width(16)) register_1 (.D(in_1), .en(in_2), .clk(clock_1_out), .Q(out_3));  // open: clr
endmodule

module register1bit (
  input  \bit ,
  input  load,
  input  ck,
  output out_4
);

  wire DFF_q, DFF_qn, multiplexer_1_out;

  D_Flip_Flop DFF (.D(multiplexer_1_out), .clk(ck), .Q(DFF_q), .Qn(DFF_qn));  // open: preset, reset
  Multiplexer multiplexer_1 (.in0(DFF_q), .in1(\bit ), .out(multiplexer_1_out), .sel(load));
  not not_1 (out_4, DFF_qn);
endmodule

module register16bit (
  input  ck,
  input  load,
  input  [15:0] word,
  output [15:0] out_4
);

  register1bit bit0 (.\bit (word[0]), .load(load), .ck(ck), .out_4(out_4[0]));
  register1bit bit1 (.\bit (word[1]), .load(load), .ck(ck), .out_4(out_4[1]));
  register1bit bit2 (.\bit (word[2]), .load(load), .ck(ck), .out_4(out_4[2]));
  register1bit bit3 (.\bit (word[3]), .load(load), .ck(ck), .out_4(out_4[3]));
  register1bit bit4 (.\bit (word[4]), .load(load), .ck(ck), .out_4(out_4[4]));
  register1bit bit5 (.\bit (word[5]), .load(load), .ck(ck), .out_4(out_4[5]));
  register1bit bit6 (.\bit (word[6]), .load(load), .ck(ck), .out_4(out_4[6]));
  register1bit bit7 (.\bit (word[7]), .load(load), .ck(ck), .out_4(out_4[7]));
  register1bit bit8 (.\bit (word[8]), .load(load), .ck(ck), .out_4(out_4[8]));
  register1bit bit9 (.\bit (word[9]), .load(load), .ck(ck), .out_4(out_4[9]));
  register1bit bit10 (.\bit (word[10]), .load(load), .ck(ck), .out_4(out_4[10]));
  register1bit bit11 (.\bit (word[11]), .load(load), .ck(ck), .out_4(out_4[11]));
  register1bit bit12 (.\bit (word[12]), .load(load), .ck(ck), .out_4(out_4[12]));
  register1bit bit13 (.\bit (word[13]), .load(load), .ck(ck), .out_4(out_4[13]));
  register1bit bit14 (.\bit (word[14]), .load(load), .ck(ck), .out_4(out_4[14]));
  register1bit bit15 (.\bit (word[15]), .load(load), .ck(ck), .out_4(out_4[15]));
endmodule

module PcCounter (
  input  ck,
  input  increment,
  input  reset,
  input  load,
  input  [15:0] word,
  output [15:0] output1
);

  wire [15:0] adder_1_out, multiplexer_1_out, multiplexer_2_out, multiplexer_3_out;

  Adder #(.width(16)) adder_1 (.a(16'h1), .b(output1), .out(adder_1_out));  // open: cin, cout
  Multiplexer #(.width(16)) multiplexer_1 (.in0(word), .in1(adder_1_out), .out(multiplexer_1_out), .sel(increment));
  Multiplexer #(.width(16)) multiplexer_2 (.in0(multiplexer_1_out), .in1(word), .out(multiplexer_2_out), .sel(load));
  Multiplexer #(.width(16)) multiplexer_3 (
    .in0(multiplexer_2_out), .in1({16{1'b0}}), .out(multiplexer_3_out), .sel(reset));
  register16bit register16bit_1 (.ck(ck), .load(1'b1), .word(multiplexer_3_out), .out_4(output1));
endmodule

module testPcCounter (
  input  in_1,
  input  in_2,
  input  in_3,
  input  [15:0] in_4,
  output [15:0] out_5
);

  wire clock_1_out;

  Clock clock_1 (.out(clock_1_out));
  PcCounter pccounter_1 (.ck(clock_1_out), .increment(in_1), .reset(in_2), .load(in_3), .word(in_4), .output1(out_5));
endmodule

module RAM8 (
  input  ck,
  input  load,
  input  [15:0] in_3,
  input  [15:0] pos,
  input  [15:0] word,
  output [15:0] out_6,
  output [15:0] out_7,
  output [15:0] out_8,
  output [15:0] out1,
  output [15:0] out_10,
  output [15:0] out_11,
  output [15:0] out_12,
  output [15:0] out_13,
  output [15:0] out_14,
  output [15:0] out_15
);

  wire demultiplexer_1_out0, demultiplexer_1_out1, demultiplexer_1_out2, demultiplexer_1_out3,
       demultiplexer_1_out4, demultiplexer_1_out5, demultiplexer_1_out6, demultiplexer_1_out7;

  Demultiplexer #(.select(3)) demultiplexer_1 (
    .out0(demultiplexer_1_out0), .out1(demultiplexer_1_out1), .out2(demultiplexer_1_out2),
    .out3(demultiplexer_1_out3), .out4(demultiplexer_1_out4), .out5(demultiplexer_1_out5),
    .out6(demultiplexer_1_out6), .out7(demultiplexer_1_out7), .in(load), .sel(pos[2:0]));
  register16bit register0 (.ck(ck), .load(demultiplexer_1_out0), .word(word), .out_4(out_6));
  register16bit register1 (.ck(ck), .load(demultiplexer_1_out1), .word(word), .out_4(out_7));
  register16bit register2 (.ck(ck), .load(demultiplexer_1_out2), .word(word), .out_4(out_8));
  register16bit register3 (.ck(ck), .load(demultiplexer_1_out3), .word(word), .out_4(out_10));
  register16bit register4 (.ck(ck), .load(demultiplexer_1_out4), .word(word), .out_4(out_12));
  register16bit register5 (.ck(ck), .load(demultiplexer_1_out5), .word(word), .out_4(out_13));
  register16bit register6 (.ck(ck), .load(demultiplexer_1_out6), .word(word), .out_4(out_14));
  register16bit register7 (.ck(ck), .load(demultiplexer_1_out7), .word(word), .out_4(out_15));
  Multiplexer #(.select(3), .width(16)) multiplexer_1 (
    .in0(out_6), .in1(out_7), .in2(out_8), .in3(out_10), .in4(out_12), .in5(out_13), .in6(out_14),
    .in7(out_15), .out(out1), .sel(pos[2:0]));
endmodule

module testRAM8 (
  input  in_1,
  input  [15:0] in_2,
  input  [15:0] in_3,
  output [15:0] out_4
);

  wire clock_1_out;

  Clock clock_1 (.out(clock_1_out));
  RAM8 ram8_1 (
    .ck(clock_1_out), .load(in_1), .in_3(in_2), .pos(in_3), .out_6(out_4));  // open: word, out_7, out_8, out1, out_10, out_11, out_12, out_13, out_14, out_15
endmodule

module testRegister16bit (
  input  in_1,
  input  [15:0] in_2,
  output [15:0] out_3
);

  wire clock_1_out;

  Clock clock_1 (.out(clock_1_out));
  register16bit register16bit_1 (.ck(clock_1_out), .load(in_1), .word(in_2), .out_4(out_3));
endmodule
